# Fritzing sketch eeprom-programmer (saved by Fritzing 0.9.10b)
breadboards: 1

parts:
  Part1 = Arduino Nano (Rev3.0) (ICSP)
  IC1 = IC, DIP package, 16 pins [chip_label=74HC595]
  IC2 = IC, DIP package, 16 pins [chip_label=74HC595]
  IC3 = IC, DIP package, 28 pins [chip_label=AT28C64]

nets:
  N1: Part1.D2, IC1.pin14
  N2: Part1.D3, IC1.pin11, IC2.pin11
  N3: Part1.D4, IC1.pin12, IC2.pin12
  N4: Part1.D5, IC3.pin11
  N5: Part1.D6, IC3.pin12
  N6: Part1.D7, IC3.pin13
  N7: Part1.D8, IC3.pin15
  N8: Part1.D9, IC3.pin16
  N9: Part1.D10, IC3.pin17
  N10: Part1.D11/MOSI, IC3.pin18
  GND: Part1.GND, IC1.pin8, IC1.pin13, IC2.pin8, IC2.pin13, IC3.pin14, IC3.pin20
  N11: Part1.A0, IC3.pin22
  N12: Part1.D12/MISO, IC3.pin19
  N13: Part1.D13/SCK, IC3.pin27
  N14: IC1.pin1, IC3.pin9
  N15: IC1.pin2, IC3.pin8
  N16: IC1.pin3, IC3.pin7
  N17: IC1.pin4, IC3.pin6
  N18: IC1.pin5, IC3.pin5
  N19: IC1.pin6, IC3.pin4
  N20: IC1.pin7, IC3.pin3
  N21: IC1.pin9, IC2.pin14
  5V: IC1.pin10, IC1.pin16, IC2.pin10, IC2.pin16, IC3.pin28
  N22: IC1.pin15, IC3.pin10
  N23: IC2.pin1, IC3.pin24
  N24: IC2.pin2, IC3.pin21
  N25: IC2.pin3, IC3.pin23
  N26: IC2.pin4, IC3.pin2
  N27: IC2.pin15, IC3.pin25
